# Fritzing sketch wiring (saved by Fritzing 0.9.3b)
breadboards: 1

parts:
  Raspberry_Pi_1 = Raspberry Pi 3 [part_number=RPI-3-V1.2]
  S1 = Pushbutton [package="[THT]"]
  S2 = Pushbutton [package="[THT]"]
  R1 = Resistor [tolerance=±5% resistance=10k package=THT]
  R2 = Resistor [tolerance=±5% resistance=10k package=THT]

nets:
  N1: Raspberry_Pi_1.GND, S1.Pin_1, S1.Pin_2, S2.Pin_1, S2.Pin_2
  N2: Raspberry_Pi_1.GIPO21, S2.Pin_3, S2.Pin_4, R1.Pin_0
  N3: Raspberry_Pi_1.GIPO20, S1.Pin_3, S1.Pin_4, R2.Pin_0
  N4: Raspberry_Pi_1.5V, R1.Pin_1, R2.Pin_1
